// Logisim project control-logic.circ as structural Verilog: 1 circuit, main circuit control_logic
module control_logic (
  input  [31:0] Instruction,
  input  BrEq,
  input  BrLt,
  output PCSel,
  output RegWEn,
  output [2:0] ImmSel,
  output BrUn,
  output ASel,
  output BSel,
  output [3:0] ALUSel,
  output MemWEn,
  output [1:0] WBSel,
  output [5:0] out_13
);

  wire and_41_out, and_42_out, and_43_out, and_44_out, BType, fun000, fun001, fun7val0, fun7val1, fun7val2,
       fun010, fun011, fun100, fun101, fun110, fun111, Gr1st, Gr2nd, Gr3rd, I1Type, I2Type, not_1_out,
       not_2_out, Op000, Op001, Op010, Op011, Op100, Op101, Op110, Op111, or_1_out, or_2_out, or_3_out,
       or_4_out, port0, port1, port2, port3, port4, port5, port6, port7, port8, port9, port10, port11,
       port12, port13, port14, port15, port16, port17, port18, port19, port20, port21, port22, port23,
       port24, port25, port26, port27, port28, port29, port30, port31, port32, port33, port35, RType, SType;
  wire [15:14] rom_1_data;

  Comparator #(.mode("unsigned"), .width(7)) comparator_1 (
    .a(Instruction[31:25]), .b(7'b0000001), .gt(fun7val2), .eq(fun7val1), .lt(fun7val0));
  Demultiplexer #(.select(3)) demultiplexer_1 (
    .out0(Op000), .out1(Op001), .out2(Op010), .out3(Op011), .out4(Op100), .out5(Op101), .out6(Op110),
    .out7(Op111), .in(1'b1), .sel(Instruction[6:4]));
  Comparator #(.mode("unsigned"), .width(4)) comparator_2 (
    .a(Instruction[3:0]), .b(4'b0111), .gt(Gr3rd), .eq(Gr2nd), .lt(Gr1st));
  ROM #(.addrWidth(6), .dataWidth(16)) rom_1 (
    .addr(out_13), .data({rom_1_data, WBSel, MemWEn, ALUSel, BSel, ASel, BrUn, ImmSel, RegWEn}));
  Demultiplexer #(.select(3)) demultiplexer_2 (
    .out0(fun000), .out1(fun001), .out2(fun010), .out3(fun011), .out4(fun100), .out5(fun101), .out6(fun110),
    .out7(fun111), .in(1'b1), .sel(Instruction[14:12]));
  and and_1 (port33, Op011, Gr2nd);
  and and_2 (port35, Op110, Gr2nd);
  and and_3 (port32, Gr2nd, Op001);
  and and_4 (port0, fun000, fun7val0, RType);
  and and_5 (port1, fun000, fun7val1, RType);
  and and_6 (port2, fun000, fun7val2, RType);
  and and_7 (port3, fun001, fun7val0, RType);
  and and_8 (port4, fun001, fun7val1, RType);
  and and_9 (port5, fun011, RType);
  and and_10 (port6, fun010, RType);
  and and_11 (port7, fun100, RType);
  and and_12 (port8, fun101, fun7val0, RType);
  and and_13 (port9, fun101, fun7val2, RType);
  and and_14 (port10, fun110, RType);
  and and_15 (port11, fun111, RType);
  and and_16 (port12, fun000, I1Type);
  and and_17 (port13, fun001, I1Type);
  and and_18 (port14, fun010, I1Type);
  and and_19 (port15, fun000, I2Type);
  and and_20 (port16, fun001, I2Type);
  and and_21 (port17, fun010, I2Type);
  and and_22 (port18, fun100, I2Type);
  and and_23 (port19, fun101, fun7val0, I2Type);
  and and_24 (port20, fun101, fun7val2, I2Type);
  and and_25 (port21, fun110, I2Type);
  and and_26 (port22, fun111, I2Type);
  and and_27 (port23, fun000, SType);
  and and_28 (port24, fun001, SType);
  and and_29 (port25, fun010, SType);
  and and_30 (port26, fun000, BType);
  and and_31 (port27, fun001, BType);
  and and_32 (port28, fun100, BType);
  and and_33 (port29, fun101, BType);
  and and_34 (port30, fun110, BType);
  and and_35 (port31, fun111, BType);
  and and_36 (RType, Op011, Gr1st);
  and and_37 (I1Type, Op000, Gr1st);
  and and_38 (I2Type, Gr1st, Op001);
  and and_39 (SType, Op010, Gr1st);
  and and_40 (BType, Gr1st, Op110);
  not not_1 (not_1_out, BrLt);
  not not_2 (not_2_out, BrEq);
  or or_1 (or_1_out, port28, port30);
  or or_2 (or_2_out, BrEq, not_1_out);
  or or_3 (or_3_out, port29, port31);
  and and_41 (and_41_out, port26, BrEq);
  and and_42 (and_42_out, not_2_out, port27);
  and and_43 (and_43_out, BrLt, or_1_out);
  and and_44 (and_44_out, or_2_out, or_3_out);
  or or_4 (or_4_out, and_41_out, and_42_out);
  or or_5 (PCSel, or_4_out, Gr3rd, and_43_out, port35, and_44_out);
  // Priority_Encoder #(.select_enc(6)) priority_encoder_1: pin names not known; wires that end beside it: port7, port8, port9, port10, port11, port12, port13, port14, port15, port16, port17, port18, port19, port20, port21, port22, port23, port24, port25, port26, port27, port28, port29, port30, out_13, port31, port32, port33, Gr3rd, port35

  // Other names for the same wires on the sheet: OpBottom[3:0] = Instruction[3:0]; Opcode[6:0] = Instruction[6:0];
  //   Optop[2:0] = Instruction[6:4]; funct3[2:0] = Instruction[14:12]; funct7[6:0] = Instruction[31:25];
  //   RomInput[5:0] = out_13

  // Notes on the sheet:
  //   INPUTS to your circuit
  //   contents of rom_1 (hex, n*v repeats v):
  //   1001 1401 1601 1081 1481 1581 1101 1201 1281 1681 1301 1381 41 41 41 1041 10c1 1141 1241 12c1 16c1
  //   1341 13c1 842 842 842 4*2064 2074 2074 1067 17c7 2069 2041
  //   ROM FOR CONTROL LOGIC
  //   DON'T CHANGE THE LOCATIONS OF THE INPUTS AND OUTPUTS!
  //   This is only if you choose to do the ROM option
  //   OUTPUT from your circuit
  //   Reminder: If using ROM, use combinational logic for PCSel
endmodule
