// Logisim project partial-store.circ as structural Verilog: 1 circuit, main circuit partial_store
module partial_store (
  input  [31:0] Instruction,
  input  [31:0] MemAddress,
  input  [31:0] DataFromReg,
  input  MemWEn,
  output [3:0] MemWriteMask,
  output [31:0] DataToMem
);

  wire [3:0] multiplexer_1_out, shifter_1_out, shifter_2_out;
  wire [4:0] multiplier_1_out;
  wire [31:0] multiplexer_2_out, shifter_3_out, shifter_4_out;

  Shifter #(.width(4)) shifter_1 (.in(4'b0001), .\dist (MemAddress[1:0]), .out(shifter_1_out));
  Shifter #(.width(4)) shifter_2 (.in(4'b0011), .\dist (MemAddress[1:0]), .out(shifter_2_out));
  Shifter #(.width(32)) shifter_3 (.in(DataFromReg), .\dist (5'b10000), .out(shifter_3_out));
  Multiplexer #(.select(2), .width(4)) multiplexer_1 (
    .in0(shifter_1_out), .in1(shifter_2_out), .in2(4'b1111), .out(multiplexer_1_out), .sel(Instruction[13:12]));  // open: in3
  Multiplexer #(.select(2), .width(32)) multiplexer_2 (
    .in0(DataFromReg), .in2(shifter_3_out), .out(multiplexer_2_out), .sel(MemAddress[1:0]));  // open: in1, in3
  Multiplier #(.width(5)) multiplier_1 (
    .a(5'b01000), .b({3'b000, MemAddress[1:0]}), .out(multiplier_1_out));  // open: cin, cout
  Multiplexer #(.width(4)) multiplexer_3 (.in0(4'b0000), .in1(multiplexer_1_out), .out(MemWriteMask), .sel(MemWEn));
  Shifter #(.width(32)) shifter_4 (.in(DataFromReg), .\dist (multiplier_1_out), .out(shifter_4_out));
  Multiplexer #(.select(2), .width(32)) multiplexer_4 (
    .in0(shifter_4_out), .in1(multiplexer_2_out), .in2(DataFromReg), .out(DataToMem), .sel(Instruction[13:12]));  // open: in3

  // Other names for the same wires on the sheet: LastTwo[1:0] = MemAddress[1:0]; Funct3[1:0] = Instruction[13:12]

  // Notes on the sheet:
  //   INPUTS to your circuit
  //   DON'T CHANGE THE LOCATIONS OF THE INPUTS AND OUTPUTS!
  //   OUTPUT from your circuit
endmodule
