// Logisim project regfile.circ as structural Verilog: 1 circuit, main circuit regfile
module regfile (
  input  [4:0] ReadIndex1,
  input  [4:0] ReadIndex2,
  input  [4:0] WriteIndex,
  input  [31:0] WriteData,
  input  RegWEn,
  input  clk,
  output [31:0] ra,
  output [31:0] sp,
  output [31:0] t0,
  output [31:0] t1,
  output [31:0] t2,
  output [31:0] s0,
  output [31:0] s1,
  output [31:0] a0,
  output [31:0] ReadData1,
  output [31:0] ReadData2
);

  wire x1, x2, x3, x4, x5, x6, x7, x8, x9, x10, x11, x12, x13, x14, x15, x16, x17, x18, x19, x20, x21, x22,
       x23, x24, x25, x26, x27, x28, x29, x30, x31;
  wire [31:0] a1, a2, a3, a4, a5, a6, a7, gp, s2, s3, s4, s5, s6, s7, s8, s9, s10, s11, t3, t4, t5, t6, tp,
       x0, x1_in, x2_in, x3_in, x4_in, x5_in, x6_in, x7_in, x8_in, x9_in, x10_in, x11_in, x12_in, x13_in,
       x14_in, x15_in, x16_in, x17_in, x18_in, x19_in, x20_in, x21_in, x22_in, x23_in, x24_in, x25_in,
       x26_in, x27_in, x28_in, x29_in, x30_in, x31_in;

  Register #(.width(32)) register_1 (.D({32{1'b0}}), .clk(clk), .Q(x0));  // open: en, clr
  Register #(.width(32)) register_2 (.D(x4_in), .en(x4), .clk(clk), .Q(tp));  // open: clr
  Register #(.width(32)) register_3 (.D(x8_in), .en(x8), .clk(clk), .Q(s0));  // open: clr
  Register #(.width(32)) register_4 (.D(x12_in), .en(x12), .clk(clk), .Q(a2));  // open: clr
  Register #(.width(32)) register_5 (.D(x16_in), .en(x16), .clk(clk), .Q(a6));  // open: clr
  Register #(.width(32)) register_6 (.D(x20_in), .en(x20), .clk(clk), .Q(s4));  // open: clr
  Register #(.width(32)) register_7 (.D(x24_in), .en(x24), .clk(clk), .Q(s8));  // open: clr
  Register #(.width(32)) register_8 (.D(x28_in), .en(x28), .clk(clk), .Q(t3));  // open: clr
  Register #(.width(32)) register_9 (.D(x1_in), .en(x1), .clk(clk), .Q(ra));  // open: clr
  Register #(.width(32)) register_10 (.D(x5_in), .en(x5), .clk(clk), .Q(t0));  // open: clr
  Register #(.width(32)) register_11 (.D(x9_in), .en(x9), .clk(clk), .Q(s1));  // open: clr
  Register #(.width(32)) register_12 (.D(x13_in), .en(x13), .clk(clk), .Q(a3));  // open: clr
  Register #(.width(32)) register_13 (.D(x17_in), .en(x17), .clk(clk), .Q(a7));  // open: clr
  Register #(.width(32)) register_14 (.D(x21_in), .en(x21), .clk(clk), .Q(s5));  // open: clr
  Register #(.width(32)) register_15 (.D(x25_in), .en(x25), .clk(clk), .Q(s9));  // open: clr
  Register #(.width(32)) register_16 (.D(x29_in), .en(x29), .clk(clk), .Q(t4));  // open: clr
  Register #(.width(32)) register_17 (.D(x6_in), .en(x6), .clk(clk), .Q(t1));  // open: clr
  Register #(.width(32)) register_18 (.D(x10_in), .en(x10), .clk(clk), .Q(a0));  // open: clr
  Register #(.width(32)) register_19 (.D(x14_in), .en(x14), .clk(clk), .Q(a4));  // open: clr
  Register #(.width(32)) register_20 (.D(x18_in), .en(x18), .clk(clk), .Q(s2));  // open: clr
  Register #(.width(32)) register_21 (.D(x22_in), .en(x22), .clk(clk), .Q(s6));  // open: clr
  Register #(.width(32)) register_22 (.D(x26_in), .en(x26), .clk(clk), .Q(s10));  // open: clr
  Register #(.width(32)) register_23 (.D(x30_in), .en(x30), .clk(clk), .Q(t5));  // open: clr
  Register #(.width(32)) register_24 (.D(x2_in), .en(x2), .clk(clk), .Q(sp));  // open: clr
  Register #(.width(32)) register_25 (.D(x11_in), .en(x11), .clk(clk), .Q(a1));  // open: clr
  Register #(.width(32)) register_26 (.D(x15_in), .en(x15), .clk(clk), .Q(a5));  // open: clr
  Register #(.width(32)) register_27 (.D(x19_in), .en(x19), .clk(clk), .Q(s3));  // open: clr
  Register #(.width(32)) register_28 (.D(x23_in), .en(x23), .clk(clk), .Q(s7));  // open: clr
  Register #(.width(32)) register_29 (.D(x27_in), .en(x27), .clk(clk), .Q(s11));  // open: clr
  Register #(.width(32)) register_30 (.D(x31_in), .en(x31), .clk(clk), .Q(t6));  // open: clr
  Register #(.width(32)) register_31 (.D(x3_in), .en(x3), .clk(clk), .Q(gp));  // open: clr
  Register #(.width(32)) register_32 (.D(x7_in), .en(x7), .clk(clk), .Q(t2));  // open: clr
  Multiplexer #(.select(5), .width(32)) multiplexer_1 (
    .in0(x0), .in1(ra), .in2(sp), .in3(gp), .in4(tp), .in5(t0), .in6(t1), .in7(t2), .in8(s0), .in9(s1),
    .in10(a0), .in11(a1), .in12(a2), .in13(a3), .in14(a4), .in15(a5), .in16(a6), .in17(a7), .in18(s2),
    .in19(s3), .in20(s4), .in21(s5), .in22(s6), .in23(s7), .in24(s8), .in25(s9), .in26(s10), .in27(s11),
    .in28(t3), .in29(t4), .in30(t5), .in31(t6), .out(ReadData1), .sel(ReadIndex1));
  Demultiplexer #(.select(5), .width(32)) demultiplexer_1 (
    .out1(x1_in), .out2(x2_in), .out3(x3_in), .out4(x4_in), .out5(x5_in), .out6(x6_in), .out7(x7_in),
    .out8(x8_in), .out9(x9_in), .out10(x10_in), .out11(x11_in), .out12(x12_in), .out13(x13_in),
    .out14(x14_in), .out15(x15_in), .out16(x16_in), .out17(x17_in), .out18(x18_in), .out19(x19_in),
    .out20(x20_in), .out21(x21_in), .out22(x22_in), .out23(x23_in), .out24(x24_in), .out25(x25_in),
    .out26(x26_in), .out27(x27_in), .out28(x28_in), .out29(x29_in), .out30(x30_in), .out31(x31_in),
    .in(WriteData), .sel(WriteIndex));  // open: out0
  Multiplexer #(.select(5), .width(32)) multiplexer_2 (
    .in0(x0), .in1(ra), .in2(sp), .in3(gp), .in4(tp), .in5(t0), .in6(t1), .in7(t2), .in8(s0), .in9(s1),
    .in10(a0), .in11(a1), .in12(a2), .in13(a3), .in14(a4), .in15(a5), .in16(a6), .in17(a7), .in18(s2),
    .in19(s3), .in20(s4), .in21(s5), .in22(s6), .in23(s7), .in24(s8), .in25(s9), .in26(s10), .in27(s11),
    .in28(t3), .in29(t4), .in30(t5), .in31(t6), .out(ReadData2), .sel(ReadIndex2));
  Demultiplexer #(.select(5)) demultiplexer_2 (
    .out1(x1), .out2(x2), .out3(x3), .out4(x4), .out5(x5), .out6(x6), .out7(x7), .out8(x8), .out9(x9),
    .out10(x10), .out11(x11), .out12(x12), .out13(x13), .out14(x14), .out15(x15), .out16(x16), .out17(x17),
    .out18(x18), .out19(x19), .out20(x20), .out21(x21), .out22(x22), .out23(x23), .out24(x24), .out25(x25),
    .out26(x26), .out27(x27), .out28(x28), .out29(x29), .out30(x30), .out31(x31), .in(RegWEn),
    .sel(WriteIndex));  // open: out0

  // Notes on the sheet:
  //   INPUTS to your circuit
  //   DON'T CHANGE THE LOCATIONS OF THE INPUTS AND OUTPUTS!
  //   These are DEBUG/TEST outputs from your circuit.
  //   OUTPUTS from your circuit
endmodule
